// Logisim project TrabalhoPraticoU1.circ as structural Verilog: 4 circuits, main circuit main
module main (
  input  A0,
  input  A1,
  input  A2,
  input  B0,
  input  B1,
  input  B2
);

  wire clock_1_out, conversor7segmentos_1_a, conversor7segmentos_1_b, conversor7segmentos_1_c,
       conversor7segmentos_1_d, conversor7segmentos_1_e, conversor7segmentos_1_f, conversor7segmentos_1_g,
       registrador3bits_1_q0, registrador3bits_1_q1, registrador3bits_1_q2, somador3bits_1_s0,
       somador3bits_1_s1, somador3bits_1_s2;

  Somador3Bits somador3bits_1 (
    .A2(A2), .B2(B2), .A1(A1), .B1(B1), .A0(A0), .B0(B0), .S2(somador3bits_1_s2), .S1(somador3bits_1_s1),
    .S0(somador3bits_1_s0));  // open: C2
  Clock clock_1 (.out(clock_1_out));
  Registrador3Bits registrador3bits_1 (
    .CLK(clock_1_out), .D0(somador3bits_1_s2), .D1(somador3bits_1_s1), .D2(somador3bits_1_s0),
    .Q0(registrador3bits_1_q0), .Q1(registrador3bits_1_q1), .Q2(registrador3bits_1_q2));
  Conversor7Segmentos conversor7segmentos_1 (
    .In0(registrador3bits_1_q0), .In1(registrador3bits_1_q1), .In2(registrador3bits_1_q2),
    .a(conversor7segmentos_1_a), .b(conversor7segmentos_1_b), .c(conversor7segmentos_1_c),
    .d(conversor7segmentos_1_d), .e(conversor7segmentos_1_e), .f(conversor7segmentos_1_f),
    .g(conversor7segmentos_1_g));
  _7_Segment_Display u_7_segment_display_1 (
    .g(conversor7segmentos_1_a), .f(conversor7segmentos_1_b), .a(conversor7segmentos_1_c),
    .b(conversor7segmentos_1_d), .e(conversor7segmentos_1_e), .d(conversor7segmentos_1_f),
    .c(conversor7segmentos_1_g));  // open: dp
endmodule

module Somador3Bits (
  input  A2,
  input  B2,
  input  A1,
  input  B1,
  input  A0,
  input  B0,
  output S2,
  output C2,
  output S1,
  output S0
);

  wire and_1_out, and_2_out, and_3_out, and_4_out, and_5_out, or_2_out, xor_1_out, xor_2_out;

  xor xor_1 (xor_1_out, A2, B2);
  and and_1 (and_1_out, A2, B2);
  xor xor_2 (xor_2_out, A1, B1);
  and and_2 (and_2_out, A1, B1);
  xor xor_3 (S0, A0, B0);
  and and_3 (and_3_out, A0, B0);
  xor xor_4 (S2, xor_1_out, or_2_out);
  and and_4 (and_4_out, xor_1_out, or_2_out);
  xor xor_5 (S1, xor_2_out, and_3_out);
  and and_5 (and_5_out, xor_2_out, and_3_out);
  or or_1 (C2, and_4_out, and_1_out);
  or or_2 (or_2_out, and_5_out, and_2_out);
endmodule

module Registrador3Bits (
  input  CLK,
  input  D0,
  input  D1,
  input  D2,
  output Q0,
  output Q1,
  output Q2
);

  D_Flip_Flop d_ff_1 (.D(D0), .clk(CLK), .Q(Q0));  // open: Qn, preset, reset
  D_Flip_Flop d_ff_2 (.D(D1), .clk(CLK), .Q(Q1));  // open: Qn, preset, reset
  D_Flip_Flop d_ff_3 (.D(D2), .clk(CLK), .Q(Q2));  // open: Qn, preset, reset
endmodule

module Conversor7Segmentos (
  input  In0,
  input  In1,
  input  In2,
  output a,
  output b,
  output c,
  output d,
  output e,
  output f,
  output g
);

  wire and_1_out, and_2_out, and_3_out, and_4_out, and_5_out, and_6_out, and_7_out, and_8_out, and_9_out,
       and_10_out, and_11_out, and_12_out, and_13_out, and_14_out, and_15_out, and_16_out, not_1_out,
       not_2_out, not_3_out;

  not not_1 (not_1_out, In0);
  not not_2 (not_2_out, In1);
  not not_3 (not_3_out, In2);
  and and_1 (and_1_out, not_1_out, In1);
  and and_2 (and_2_out, In0, not_2_out);
  or or_1 (a, and_1_out, and_2_out, and_3_out);
  and and_3 (and_3_out, In1, not_3_out);
  and and_4 (and_4_out, not_2_out, not_3_out);
  and and_5 (and_5_out, In0, not_2_out);
  or or_2 (b, and_4_out, and_5_out, and_6_out);
  and and_6 (and_6_out, In0, not_3_out);
  and and_7 (and_7_out, not_1_out, not_3_out);
  or or_3 (c, and_7_out, In1, and_8_out);
  and and_8 (and_8_out, In0, In2);
  and and_9 (and_9_out, not_2_out, not_3_out);
  or or_4 (d, not_1_out, and_9_out, and_10_out);
  and and_10 (and_10_out, In1, In2);
  and and_11 (and_11_out, not_1_out, not_3_out);
  or or_5 (e, and_11_out, and_12_out);
  and and_12 (and_12_out, In1, not_3_out);
  and and_13 (and_13_out, not_1_out, not_3_out);
  and and_14 (and_14_out, not_1_out, In1);
  and and_15 (and_15_out, In0, not_2_out, In2);
  and and_16 (and_16_out, In1, not_3_out);
  or or_6 (g, not_2_out, In2, In0);
  or or_7 (f, and_13_out, and_14_out, and_15_out, and_16_out);
endmodule
